# Fritzing sketch fritzing-monitor-pool (saved by Fritzing 1.0.2b)
breadboards: 2

parts:
  Part2 = TinyPICO
  A1 = Waveshare e-Paper HAT [package=THT]
  Part3 = Adafruit MAX31856 Thermocouple Amp [part_number="Adafruit #3263"]
  U1 = LIPO-110mAh [package=lipo-110]
  U2 = MMA_ACCEL_CONNECTOR [package=1x08]

nets:
  3V3: Part2.3V3, A1.pin_8, Part3.VIN, U2.SLP
  N1: Part2.GND, A1.pin_7, U1.-, U2.GS2
  N2: Part2.BAT, U1.+
  N3: Part2.33, Part3.!CS
  N4: Part2.32, A1.pin_1, U2.VCC
  N5: Part2.21, A1.pin_2, U2.GND
  N6: Part2.22, A1.pin_3, U2.X
  N7: Part2.5, A1.pin_4, U2.Y
  N8: Part2.18, A1.pin_5, Part3.SCK, U2.Z
  N9: Part2.19, Part3.SDO
  N10: Part2.23, A1.pin_6, Part3.SDI, U2.GS1

custom parts:
  TinyPICO: TinyPICO ESP32 by Unexpected Maker
  Waveshare e-Paper HAT: .This is a universal driver board for e-Paper raw panels, can be used to drive various SPI interface e-Paper from Waveshare.
  Adafruit MAX31856 Thermocouple Amp: Thermocouples are very sensitive, requiring a good amplifier with a cold-compensation reference, as well as calculations to handle any non-linearities. For a long time we've suggested our MAX31855K breakout, which works great but is only for K-type thermocouples. Now we're happy to offer a great new thermocouple amplifier/converter that can handle just about any type of thermocouple, and even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
